# Fritzing sketch rgb_led_circuit (saved by Fritzing 1.0.3b)
breadboards: 1

parts:
  Mod2 = ESP32-TTGO-T-DISPLAY
  S1 = Square Pushbutton
  Part1 = Thumb Joystick
  R5 = Rotary Potentiometer (Small) [maximum_resistance=10kΩ knob_status=50% power=0.5W package=THT]
  Part2 = NeoPixel Stick [part_number=1426]
  R6 = Resistor [tolerance=±5% power=0.25W resistance=450 package=THT]

nets:
  GND: Mod2.G-1, Mod2.G-2, Mod2.G-10, Mod2.G-11, Mod2.G-14, S1.leg0, Part1.GND, R5.leg2, Part2.GND, R6.Pin_1
  N1: Mod2.17, R6.Pin_0
  N2: Mod2.2, R5.wiper
  N3: Mod2.15, Part1.SEL
  N4: Mod2.13, Part1.VERT
  N5: Mod2.12, Part1.HORZ
  5V: Mod2.5V, Part1.VCC, R5.leg1, Part2.+5V
  N6: Mod2.38, S1.leg1

custom parts:
  ESP32-TTGO-T-DISPLAY: LILYGO TTGO T-Display GD32VF103CBT6 Main Chip ST7789 1.14 Inch IPS 240x135 Resolution Minimalist Development Board.
  NeoPixel Stick: Make your own little LED strip arrangement with this stick of NeoPixel LEDs. We crammed 8 of the tiny 5050 (5mm x 5mm) smart RGB LEDs onto a PCB with mounting holes and a chainable design. Use only one microcontroller pin to control as many as you can chain together! Each LED is addressable as the driver chip is inside the LED. Each one has ~18mA constant current drive so the color will be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

// code stored in the sketch: led_controler.ino
/*
 * This ESP32 code is created by esp32io.com
 *
 * This ESP32 code is released in the public domain
 *
 * For more detail (instruction and wiring diagram), visit https://esp32io.com/tutorials/esp32-led-strip
 */

#define BLUE_PIN  7  // The ESP32 pin GPIO23 connects to the blue pin of LED strip via relay 1
#define RED_PIN   5  // The ESP32 pin GPIO22 connects to the red pin of LED strip via relay 2
#define GREEN_PIN 6  // The ESP32 pin GPIO21 connects to the green pin of LED strip via relay 3

void setup() {
  Serial.begin(9600);

  // initialize ESP32 pins as digital output pins
  pinMode(BLUE_PIN,  OUTPUT);
  pinMode(RED_PIN,   OUTPUT);
  pinMode(GREEN_PIN, OUTPUT);
}

// the loop function runs over and over again forever
void loop() {
  Serial.println("The LED strip is turned red");
  digitalWrite(BLUE_PIN,  LOW);
  digitalWrite(RED_PIN,   HIGH);
  digitalWrite(GREEN_PIN, LOW);
  delay(2000);

  Serial.println("The LED strip is turned green");
  digitalWrite(BLUE_PIN,  LOW);
  digitalWrite(RED_PIN,   LOW);
  digitalWrite(GREEN_PIN, HIGH);
  delay(2000);

  Serial.println("The LED strip is turned blue");
  digitalWrite(BLUE_PIN,  HIGH);
  digitalWrite(RED_PIN,   LOW);
  digitalWrite(GREEN_PIN, LOW);
  delay(2000);

  Serial.println("The LED strip is turned yellow");
  digitalWrite(BLUE_PIN,  LOW);
  digitalWrite(RED_PIN,   HIGH);
  digitalWrite(GREEN_PIN, HIGH);
  delay(2000);

  Serial.println("The LED strip is turned magenta");
  digitalWrite(BLUE_PIN,  HIGH);
  digitalWrite(RED_PIN,   HIGH);
  digitalWrite(GREEN_PIN, LOW);
  delay(2000);

  Serial.println("The LED strip is turned cyan");
  digitalWrite(BLUE_PIN,  HIGH);
  digitalWrite(RED_PIN,   LOW);
  digitalWrite(GREEN_PIN, HIGH);
  delay(2000);

  Serial.println("The LED strip is turned white");
  digitalWrite(BLUE_PIN,  HIGH);
  digitalWrite(RED_PIN,   HIGH);
  digitalWrite(GREEN_PIN, HIGH);
  delay(2000);
}
